# Fritzing sketch draft3 (saved by Fritzing 0.9.3b)
breadboards: 1

parts:
  Part4 = Real Time Clock Module - DS1307 RTC Breakout Board
  M6 = DC Motor
  M7 = DC Motor
  Part5 = Arduino Nano (Rev3.0)
  8_Channel_Relay4 = 8 Channel Power Relay
  RHT1 = Humidity and Temperature Sensor RHT03
  LED1 = LEDs [package=led10mm]
  Part6 = Lilypad Battery Connect

nets:
  5V: Part4.5V, Part5.5V, 8_Channel_Relay4.VCC, 8_Channel_Relay4.NC, RHT1.Vcc
  GND: Part4.GND, M6.pin_2, Part5.GND, 8_Channel_Relay4.GND, RHT1.GND_1
  N1: Part4.SCL, Part5.A4
  N2: Part4.SDA, Part5.A3
  N3: M6.pin_1, 8_Channel_Relay4.COM#40
  N4: M7.pin_1, 8_Channel_Relay4.COM#43
  N5: Part5.D2, 8_Channel_Relay4.IN1
  N6: Part5.D3, 8_Channel_Relay4.IN2
  N7: Part5.D4, 8_Channel_Relay4.IN6
  N8: Part5.D5, RHT1.Data-signal
  N9: 8_Channel_Relay4.COM#28, Part6.+
  N10: 8_Channel_Relay4.NO, LED1.C
  N11: LED1.A, Part6.-

notes:
  Relay
  DC air Pump
  Nano
  RTC Module
  Temperature and Humdity sensor
  DC water Pump
  AC Supply

custom parts:
  8 Channel Power Relay: An 8 channel power relay. The module operates at 5V.
  LEDs: LEDs Standard schematic elements and footprints for 5mm, 3mm, 1206, and 0603 sized LEDs. 5mm - Spark Fun Electronics SKU : COM-00529 (and others)
