# Fritzing sketch proto1 (saved by Fritzing 0.9.3b)
breadboards: 1

parts:
  Part1 = Arduino Nano (Rev3.0)
  U1 = Module 4 Relais 5V [package="Module 4 Relais 5V"]
  M7 = DC Motor
  RHT2 = Humidity and Temperature Sensor RHT03
  Part5 = Real Time Clock Module - DS1307 RTC Breakout Board
  Part6 = LED Matrix - Serial Interface - Red/Green/Blue
  BAT1 = BC9VPC [package=bc9vpc]

nets:
  GND: Part1.GND, U1.GND, RHT2.GND_1, Part5.GND, Part6.GND
  N1: Part1.D5, U1.IN1
  N2: Part1.D6, Part6.CS
  N3: Part1.D7, Part6.SCK
  N4: Part1.D8, Part6.VCC
  N5: Part1.D9, RHT2.Data-signal
  5V: Part1.5V, U1.VCC, RHT2.Vcc, Part5.5V, Part6.MOSI
  N6: Part1.A5, Part5.SCL
  N7: Part1.A4, Part5.SDA
  N8: U1.K1-NF, M7.pin_1
  N9: U1.K1-NO, BAT1.V+
  N10: M7.pin_2, BAT1.V-

notes:
  DC water Pump
  Relay
  Nano
  Temperature and Humdity sensor
  (DHT11)
  RTC (DS3231)
  8x8 LED Dot Matrix

custom parts:
  Module 4 Relais 5V: Module 4 Relais 5V 4x SPD-06VDC-SD-C
